# Fritzing sketch slider (saved by Fritzing 0.9.3b)
circuit board: 8.46667cm x 5.64444cm
breadboards: 1

parts:
  Arduino = Arduino Pro Mini v13
  M1 = Stepper Motor - Bipolar
  Stepper_Motor_Driver = Motor Driver 1A Dual TB6612FNG
  Start/Stop = Round Pushbutton
  R1 = Resistor [tolerance=±5% resistance=220 package=THT]
  Speed = POT [package=pot_alpha_rv16af-20]
  12v = Power Jack [package=power_jack_slot]
  S1 = Pushbutton [package=THT]
  S2 = Pushbutton [package=THT]
  R2 = Resistor [tolerance=±5% resistance=220 package=THT]
  R3 = Resistor [tolerance=±5% resistance=220 package=THT]

nets:
  N1: Arduino.DTR, Arduino.D0/TX
  GND: Arduino.GND, Stepper_Motor_Driver.GND, Start/Stop.leg1, Speed.A, 12v.GND
  N2: Arduino.A0, Speed.S
  N3: Arduino.D13/SCK, S1.leg1
  N4: Arduino.D12/MISO, S2.leg1
  N5: Arduino.D7, Stepper_Motor_Driver.BIN2
  N6: Arduino.D6_PWM, Stepper_Motor_Driver.BIN1
  N7: Arduino.D5_PWM, Stepper_Motor_Driver.AIN1
  N8: Arduino.D4, Stepper_Motor_Driver.AIN2
  N9: Arduino.D2, R1.Pin_1
  N10: M1.A, Stepper_Motor_Driver.A01
  N11: M1.C, Stepper_Motor_Driver.A02
  N12: M1.B, Stepper_Motor_Driver.B01
  N13: M1.D, Stepper_Motor_Driver.B02
  N14: Stepper_Motor_Driver.VCC, Speed.E, R2.Pin_0, R3.Pin_0
  N15: Stepper_Motor_Driver.PWMA, Stepper_Motor_Driver.PWMB, 12v.PWR
  N16: Start/Stop.leg0, R1.Pin_0
  N17: S1.leg0, R2.Pin_1
  N18: S2.leg0, R3.Pin_1
